# Fritzing sketch TMP36_ADC_LCD (saved by Fritzing 0.9.2b)
breadboards: 1

parts:
  LCD1 = LCD screen
  U1 = TMP36 [package=to-92]
  IC1 = MCP3008 [package="DIP16 [THT]"]
  Raspberry_Pi1 = Raspberry Pi B+

nets:
  GND: LCD1.VSS, LCD1.V0, LCD1.R/W, LCD1.LED-, U1.GND, Raspberry_Pi1.GND
  VDD: LCD1.VDD, LCD1.LED+, U1.VCC, IC1.VREF, IC1.VDD, Raspberry_Pi1.3v3
  N1: LCD1.RS, Raspberry_Pi1.GPIO14
  N2: LCD1.E, Raspberry_Pi1.GPIO15
  N3: LCD1.DB4, Raspberry_Pi1.GPIO17
  N4: LCD1.DB5, Raspberry_Pi1.GPIO18
  N5: LCD1.DB6, Raspberry_Pi1.GPIO27
  N6: LCD1.DB7, Raspberry_Pi1.GPIO22
  N7: U1.VOUT, IC1.CH1
  N8: IC1.CS/SHDN, Raspberry_Pi1.GPIO19
  N9: IC1.DIN, Raspberry_Pi1.GPIO13
  N10: IC1.DOUT, Raspberry_Pi1.GPIO6
  N11: IC1.CLK, Raspberry_Pi1.GPIO5

custom parts:
  MCP3008: 2.7V 8-Channel 10-Bit A/D Converters with SPI Serial Interface
